// Logisim project cpu.circ as structural Verilog: 1 circuit, main circuit cpu
module cpu (
  input  clk,
  input  [31:0] Instruction,
  input  [31:0] MemReadData,
  output [31:0] MemAddress,
  output [31:0] ProgramCounter,
  output [31:0] ra,
  output [31:0] sp,
  output [31:0] t0,
  output [31:0] t1,
  output [31:0] t2,
  output [31:0] s0,
  output [31:0] s1,
  output [31:0] a0,
  output [3:0] MemWriteMask,
  output [31:0] MemWriteData
);

  wire [31:0] adder_1_out, alu_result, immediate, regfile_1_readdata1;

  Register #(.width(32)) PC (.D(adder_1_out), .clk(clk), .Q(ProgramCounter));  // open: en, clr
  Adder #(.width(32)) adder_1 (.a(ProgramCounter), .b(32'h4), .out(adder_1_out));  // open: cin, cout
  // control_logic control_logic_1: pin names not known
  regfile regfile_1 (
    .ReadIndex1(Instruction[19:15]), .WriteIndex(Instruction[11:7]), .WriteData(alu_result), .RegWEn(1'b1),
    .clk(clk), .ra(ra), .sp(sp), .t0(t0), .t1(t1), .t2(t2), .s0(s0), .s1(s1), .a0(a0),
    .ReadData1(regfile_1_readdata1));  // open: ReadIndex2, ReadData2
  imm_gen imm_gen_1 (.Instruction(Instruction), .Immediate(immediate));  // open: ImmSel
  alu alu_1 (.A(regfile_1_readdata1), .B(immediate), .ALUSel(4'b0000), .ALUResult(alu_result));
  // branch_comp branch_comp_1: pin names not known
  // partial_store partial_store_1: pin names not known
  // partial_load partial_load_1: pin names not known

  // Other names for the same wires on the sheet: opcode[6:0] = Instruction[6:0]; imm4_1_11[4:0] = Instruction[11:7];
  //   imm_4_0[4:0] = Instruction[11:7]; rd[4:0] = Instruction[11:7]; funct3[2:0] = Instruction[14:12];
  //   imm_20_10_1_11_19_12[19:0] = Instruction[31:12]; imm_31_12[19:0] = Instruction[31:12];
  //   rs1[4:0] = Instruction[19:15]; imm[11:0] = Instruction[31:20]

  // Notes on the sheet:
  //   To IMEM
  //   IMEM (do **NOT** move this)
  //   From IMEM
  //   Inputs/Outputs for testing. Do **NOT** move these.
  //   It is OK to move the PC, RegFile, ALU, MEM, Branch Comp, Imm Gen, Partial Load, Partial Store and Control Logic to wherever is most convenient for you when constructing your CPU, and to delete this text
  //   To DMEM
  //   DMEM (do **NOT** move this)
  //   From DMEM
endmodule
